// Logisim project ControlUnit.circ as structural Verilog: 2 circuits, main circuit ControlUnit
module ControlUnit (
  input  [31:0] OP,
  input  CLOCK,
  output WR_PC,
  output WR_RD,
  output out_5,
  output out_6,
  output out_7,
  output out_8,
  output out_9,
  output out_10,
  output out_11,
  output out_12,
  output out_13,
  output out_14,
  output out_15,
  output out_16,
  output out_17
);

  wire multiplexer_2_out;
  wire [15:0] multiplexer_1_out, optoaddr_1_nextop_addr, register_1_q, rom_1_data;
  wire [15:15] rom_1_data_2;

  Register #(.width(16)) register_1 (.D(rom_1_data), .en(1'b1), .clk(CLOCK), .Q(register_1_q));  // open: clr
  OpToAddr optoaddr_1 (.OP(OP), .NextOp_Addr(optoaddr_1_nextop_addr));
  Multiplexer #(.width(16)) multiplexer_1 (
    .in0(optoaddr_1_nextop_addr), .in1(register_1_q), .out(multiplexer_1_out), .sel(multiplexer_2_out));
  Multiplexer multiplexer_2 (.in0(1'b0), .in1(rom_1_data_2[15]), .out(multiplexer_2_out), .sel(1'b1));
  ROM #(.addrWidth(16), .dataWidth(32)) rom_1 (
    .addr(multiplexer_1_out),
    .data({rom_1_data, rom_1_data_2[15], out_17, out_16, out_15, out_14, out_13, out_12, out_11, out_10, out_9, out_8, out_7, out_6, out_5, WR_RD, WR_PC}));

  // Notes on the sheet:
  //   Init
endmodule

module OpToAddr (
  input  [31:0] OP,
  output [15:0] NextOp_Addr
);

  ROM #(.dataWidth(16)) rom_1 (.addr(OP[31:24]), .data(NextOp_Addr));
endmodule
