// Logisim project M32.circ as structural Verilog
module PC (
  input  [31:0] INPT,
  input  WR,
  output [31:0] OUTPT
);

  wire CLK_out;
  wire [31:0] register_1_q;

  Clock CLK (.out(CLK_out));
  Register #(.width(32)) register_1 (.D(INPT), .en(WR), .clk(CLK_out), .Q(register_1_q));  // open: clr
  Multiplexer #(.width(32)) multiplexer_1 (.in0({32{1'b0}}), .in1(register_1_q), .out(OUTPT));  // open: sel

  // Notes on the sheet:
  //   Programar gnd_vcc
endmodule

module RBANK (
  input  [31:0] Rd,
  input  CLK,
  input  [4:0] s1,
  input  [4:0] s2,
  input  WR,
  input  [4:0] d
);

  wire decoder_1_out0, decoder_1_out1, decoder_1_out2, decoder_1_out3, decoder_1_out4, decoder_1_out5,
       decoder_1_out6, decoder_1_out7, decoder_1_out8, decoder_1_out9, decoder_1_out10, decoder_1_out11,
       decoder_1_out12, decoder_1_out13, decoder_1_out14, decoder_1_out15, decoder_1_out16, decoder_1_out17,
       decoder_1_out18, decoder_1_out19, decoder_1_out20, decoder_1_out21, decoder_1_out22, decoder_1_out23,
       decoder_1_out24, decoder_1_out25, decoder_1_out26, decoder_1_out27, decoder_1_out28, decoder_1_out29,
       decoder_1_out30, decoder_1_out31;
  wire [31:0] register_1_q, register_2_q, register_3_q, register_4_q, register_5_q, register_6_q,
       register_7_q, register_8_q, register_9_q, register_10_q, register_11_q, register_12_q, register_13_q,
       register_14_q, register_15_q, register_16_q, register_17_q, register_18_q, register_19_q,
       register_20_q, register_21_q, register_22_q, register_23_q, register_24_q, register_25_q,
       register_26_q, register_27_q, register_28_q, register_29_q, register_30_q, register_31_q,
       register_32_q;

  Decoder #(.select(5)) decoder_1 (
    .out0(decoder_1_out0), .out1(decoder_1_out1), .out2(decoder_1_out2), .out3(decoder_1_out3),
    .out4(decoder_1_out4), .out5(decoder_1_out5), .out6(decoder_1_out6), .out7(decoder_1_out7),
    .out8(decoder_1_out8), .out9(decoder_1_out9), .out10(decoder_1_out10), .out11(decoder_1_out11),
    .out12(decoder_1_out12), .out13(decoder_1_out13), .out14(decoder_1_out14), .out15(decoder_1_out15),
    .out16(decoder_1_out16), .out17(decoder_1_out17), .out18(decoder_1_out18), .out19(decoder_1_out19),
    .out20(decoder_1_out20), .out21(decoder_1_out21), .out22(decoder_1_out22), .out23(decoder_1_out23),
    .out24(decoder_1_out24), .out25(decoder_1_out25), .out26(decoder_1_out26), .out27(decoder_1_out27),
    .out28(decoder_1_out28), .out29(decoder_1_out29), .out30(decoder_1_out30), .out31(decoder_1_out31),
    .sel(d), .en(WR));
  Register #(.width(32)) register_1 (.D(Rd), .en(decoder_1_out0), .clk(CLK), .Q(register_1_q));  // open: clr
  Register #(.width(32)) register_2 (.D(Rd), .en(decoder_1_out1), .clk(CLK), .Q(register_2_q));  // open: clr
  Register #(.width(32)) register_3 (.D(Rd), .en(decoder_1_out2), .clk(CLK), .Q(register_3_q));  // open: clr
  Register #(.width(32)) register_4 (.D(Rd), .en(decoder_1_out3), .clk(CLK), .Q(register_4_q));  // open: clr
  Register #(.width(32)) register_5 (.D(Rd), .en(decoder_1_out4), .clk(CLK), .Q(register_5_q));  // open: clr
  Register #(.width(32)) register_6 (.D(Rd), .en(decoder_1_out5), .clk(CLK), .Q(register_6_q));  // open: clr
  Register #(.width(32)) register_7 (.D(Rd), .en(decoder_1_out6), .clk(CLK), .Q(register_7_q));  // open: clr
  Register #(.width(32)) register_8 (.D(Rd), .en(decoder_1_out7), .clk(CLK), .Q(register_8_q));  // open: clr
  Register #(.width(32)) register_9 (.D(Rd), .en(decoder_1_out8), .clk(CLK), .Q(register_9_q));  // open: clr
  Register #(.width(32)) register_10 (.D(Rd), .en(decoder_1_out9), .clk(CLK), .Q(register_10_q));  // open: clr
  Register #(.width(32)) register_11 (.D(Rd), .en(decoder_1_out10), .clk(CLK), .Q(register_11_q));  // open: clr
  Register #(.width(32)) register_12 (.D(Rd), .en(decoder_1_out11), .clk(CLK), .Q(register_12_q));  // open: clr
  Register #(.width(32)) register_13 (.D(Rd), .en(decoder_1_out12), .clk(CLK), .Q(register_13_q));  // open: clr
  Register #(.width(32)) register_14 (.D(Rd), .en(decoder_1_out13), .clk(CLK), .Q(register_14_q));  // open: clr
  Register #(.width(32)) register_15 (.D(Rd), .en(decoder_1_out14), .clk(CLK), .Q(register_15_q));  // open: clr
  Register #(.width(32)) register_16 (.D(Rd), .en(decoder_1_out15), .clk(CLK), .Q(register_16_q));  // open: clr
  Register #(.width(32)) register_17 (.D(Rd), .en(decoder_1_out16), .clk(CLK), .Q(register_17_q));  // open: clr
  Register #(.width(32)) register_18 (.D(Rd), .en(decoder_1_out17), .clk(CLK), .Q(register_18_q));  // open: clr
  Register #(.width(32)) register_19 (.D(Rd), .en(decoder_1_out18), .clk(CLK), .Q(register_19_q));  // open: clr
  Register #(.width(32)) register_20 (.D(Rd), .en(decoder_1_out19), .clk(CLK), .Q(register_20_q));  // open: clr
  Register #(.width(32)) register_21 (.D(Rd), .en(decoder_1_out20), .clk(CLK), .Q(register_21_q));  // open: clr
  Register #(.width(32)) register_22 (.D(Rd), .en(decoder_1_out21), .clk(CLK), .Q(register_22_q));  // open: clr
  Register #(.width(32)) register_23 (.D(Rd), .en(decoder_1_out22), .clk(CLK), .Q(register_23_q));  // open: clr
  Register #(.width(32)) register_24 (.D(Rd), .en(decoder_1_out23), .clk(CLK), .Q(register_24_q));  // open: clr
  Register #(.width(32)) register_25 (.D(Rd), .en(decoder_1_out24), .clk(CLK), .Q(register_25_q));  // open: clr
  Register #(.width(32)) register_26 (.D(Rd), .en(decoder_1_out25), .clk(CLK), .Q(register_26_q));  // open: clr
  Register #(.width(32)) register_27 (.D(Rd), .en(decoder_1_out26), .clk(CLK), .Q(register_27_q));  // open: clr
  Register #(.width(32)) register_28 (.D(Rd), .en(decoder_1_out27), .clk(CLK), .Q(register_28_q));  // open: clr
  Register #(.width(32)) register_29 (.D(Rd), .en(decoder_1_out28), .clk(CLK), .Q(register_29_q));  // open: clr
  Register #(.width(32)) register_30 (.D(Rd), .en(decoder_1_out29), .clk(CLK), .Q(register_30_q));  // open: clr
  Register #(.width(32)) register_31 (.D(Rd), .en(decoder_1_out30), .clk(CLK), .Q(register_31_q));  // open: clr
  Register #(.width(32)) register_32 (.D(Rd), .en(decoder_1_out31), .clk(CLK), .Q(register_32_q));  // open: clr
  Multiplexer #(.select(5), .width(32)) multiplexer_1 (
    .in0(register_1_q), .in1(register_2_q), .in2(register_3_q), .in3(register_4_q), .in4(register_5_q),
    .in5(register_6_q), .in6(register_7_q), .in7(register_8_q), .in8(register_9_q), .in9(register_10_q),
    .in10(register_11_q), .in11(register_12_q), .in12(register_13_q), .in13(register_14_q),
    .in14(register_15_q), .in15(register_16_q), .in16(register_17_q), .in17(register_18_q),
    .in18(register_19_q), .in19(register_20_q), .in20(register_21_q), .in21(register_22_q),
    .in22(register_23_q), .in23(register_24_q), .in24(register_25_q), .in25(register_26_q),
    .in26(register_27_q), .in27(register_28_q), .in28(register_29_q), .in29(register_30_q),
    .in30(register_31_q), .in31(register_32_q), .sel(s2));  // open: out
  Multiplexer #(.select(5), .width(32)) multiplexer_2 (
    .in0(register_1_q), .in1(register_2_q), .in2(register_3_q), .in3(register_4_q), .in4(register_5_q),
    .in5(register_6_q), .in6(register_7_q), .in7(register_8_q), .in8(register_9_q), .in9(register_10_q),
    .in10(register_11_q), .in11(register_12_q), .in12(register_13_q), .in13(register_14_q),
    .in14(register_15_q), .in15(register_16_q), .in16(register_17_q), .in17(register_18_q),
    .in18(register_19_q), .in19(register_20_q), .in20(register_21_q), .in21(register_22_q),
    .in22(register_23_q), .in23(register_24_q), .in24(register_25_q), .in25(register_26_q),
    .in26(register_27_q), .in27(register_28_q), .in28(register_29_q), .in29(register_30_q),
    .in30(register_31_q), .in31(register_32_q), .sel(s1));  // open: out
endmodule

module BRANCHUNIT (
  input  [3:0] in_1
);

  // NOT_Gate not_1 has open pins: in=in_1[0], out=open
  // NOT_Gate not_2 has open pins: in=in_1[1], out=open
  // NOT_Gate not_3 has open pins: in=in_1[2], out=open
  // NOT_Gate not_4 has open pins: in=in_1[3], out=open
endmodule
